// Digital circuit active-1.dig as structural Verilog
module active_1 (
  input  in,
  input  act,
  output out
);

  Multiplexer multiplexer_1 (.sel(act), .in_0(1'b0), .in_1(in), .out(out));
endmodule
