// Digital circuit active-64.dig as structural Verilog
module active_64 (
  input  [63:0] in,
  input  act,
  output [63:0] out
);

  Multiplexer #(.Bits(64)) multiplexer_1 (.sel(act), .in_0({64{1'b0}}), .in_1(in), .out(out));
endmodule
