// Digital circuit active-8.dig as structural Verilog
module active_8 (
  input  [7:0] in,
  input  act,
  output [7:0] out
);

  Multiplexer #(.Bits(8)) multiplexer_1 (.sel(act), .in_0({8{1'b0}}), .in_1(in), .out(out));
endmodule
