// Digital circuit mode-merger.dig as structural Verilog
module mode_merger (
  input  [1:0] mode_1,
  input  [1:0] mode_2,
  output [1:0] mode
);

  wire comparator_1_eq;

  Comparator #(.Bits(2)) comparator_1 (.a(mode_1), .b(2'b00), .eq(comparator_1_eq));  // open: gt, lt
  Multiplexer #(.Bits(2)) multiplexer_1 (.sel(comparator_1_eq), .in_0(mode_2), .in_1(mode_1), .out(mode));
endmodule
