// Digital circuit ram-input-merger.dig as structural Verilog
module ram_input_merger (
  input  [63:0] in_1,
  input  [63:0] in_2,
  input  [63:0] in_3,
  input  [63:0] in_4,
  input  in_5,
  input  dir,
  input  [63:0] alt_1,
  input  [63:0] alt_2,
  input  [63:0] alt_3,
  input  [63:0] alt_4,
  input  alt_5,
  output [63:0] out_1,
  output [63:0] out_2,
  output [63:0] out_3,
  output [63:0] out_4,
  output out_5
);

  Multiplexer multiplexer_1 (.sel(dir), .in_0(in_5), .in_1(alt_5), .out(out_5));
  Multiplexer #(.Bits(64)) multiplexer_2 (.sel(dir), .in_0(in_4), .in_1(alt_4), .out(out_4));
  Multiplexer #(.Bits(64)) multiplexer_3 (.sel(dir), .in_0(in_3), .in_1(alt_3), .out(out_3));
  Multiplexer #(.Bits(64)) multiplexer_4 (.sel(dir), .in_0(in_1), .in_1(alt_1), .out(out_1));
  Multiplexer #(.Bits(64)) multiplexer_5 (.sel(dir), .in_0(in_2), .in_1(alt_2), .out(out_2));
endmodule
