// Digital circuit rgrm-merger.dig as structural Verilog
module rgrm_merger (
  input  rm_5,
  input  [63:0] rm_4,
  input  [63:0] rm_3,
  input  [63:0] rm_2,
  input  [63:0] rm_1,
  input  rg_5,
  input  [63:0] rg_4,
  input  [7:0] rg_3,
  input  [7:0] rg_2,
  input  [7:0] rg_1,
  input  RM_5_2,
  input  [63:0] RM_4_2,
  input  [63:0] RM_3_2,
  input  [63:0] RM_2_2,
  input  [63:0] RM_1_2,
  input  RG_5_2,
  input  [63:0] RG_4_2,
  input  [7:0] RG_3_2,
  input  [7:0] RG_2_2,
  input  [7:0] RG_1_2,
  input  dir,
  output [7:0] gr_1,
  output [7:0] gr_2,
  output [7:0] gr_3,
  output [63:0] gr_4,
  output gr_5,
  output [63:0] mr_1,
  output [63:0] mr_2,
  output [63:0] mr_3,
  output [63:0] mr_4,
  output mr_5
);

  ram_input_merger ram_input_merger_1 (
    .out_5(mr_5), .out_4(mr_4), .out_3(mr_3), .out_2(mr_2), .out_1(mr_1), .in_5(rm_5), .in_4(rm_4),
    .in_3(rm_3), .in_2(rm_2), .in_1(rm_1), .dir(dir), .alt_1(RM_1_2), .alt_2(RM_2_2), .alt_3(RM_3_2),
    .alt_4(RM_4_2), .alt_5(RM_5_2));
  registers_input_merger registers_input_merger_1 (
    .out_5(gr_5), .out_4(gr_4), .out_3(gr_3), .out_2(gr_2), .out_1(gr_1), .in_5(rg_5), .in_4(rg_4),
    .in_3(rg_3), .in_2(rg_2), .in_1(rg_1), .dir(dir), .alt_1(RG_1_2), .alt_2(RG_2_2), .alt_3(RG_3_2),
    .alt_4(RG_4_2), .alt_5(RG_5_2));
endmodule
