// Digital circuit fetcher.dig as structural Verilog
module fetcher (
  input  [1:0] mode,
  input  [63:0] IP,
  input  [63:0] word1,
  input  [63:0] word,
  input  clock,
  output act,
  output [7:0] reg_read1,
  output [63:0] ram_addr1,
  output [2:0] im_addr,
  output [63:0] im_word,
  output im_store,
  output [7:0] write_reg,
  output [63:0] write_data,
  output write_store,
  output [1:0] mode_out
);

  wire and_1_out, comparator_1_eq, comparator_2_eq, comparator_2_lt, comparator_4_lt, comparator_6_lt,
       comparator_7_eq, comparator_8_eq, not_1_out, or_1_out;
  wire [0:0] comparator_5_eq;
  wire [1:0] add_2_s;
  wire [63:0] multiplexer_1_out, register_1_q;

  Comparator #(.Bits(2)) comparator_1 (.a(mode), .b(2'b00), .eq(comparator_1_eq));  // open: gt, lt
  Register #(.Bits(64)) register_1 (.D(word1), .C(clock), .en(comparator_1_eq), .Q(register_1_q));
  Multiplexer #(.Bits(64)) multiplexer_1 (
    .sel(comparator_1_eq), .in_0(register_1_q), .in_1(word1), .out(multiplexer_1_out));
  Comparator #(.Bits(2)) comparator_2 (.a(mode), .b(2'b10), .eq(comparator_2_eq), .lt(comparator_2_lt));  // open: gt
  and and_1 (and_1_out, comparator_2_lt, clock);
  Counter #(.Bits(3)) counter_1 (.en(1'b1), .C(and_1_out), .clr(or_1_out), .out(im_addr));  // open: ovf
  or or_1 (or_1_out, comparator_2_eq, comparator_7_eq, write_store);
  Comparator #(.Bits(3)) comparator_3 (.a(multiplexer_1_out[2:0]), .b(im_addr), .eq(write_store));  // open: gt, lt
  Comparator #(.Bits(2)) comparator_4 (.a(mode), .b(2'b00), .lt(comparator_4_lt));  // open: gt, eq
  Multiplexer #(.Bits(64)) multiplexer_2 (.sel(comparator_4_lt), .in_0(write_data), .in_1(IP), .out(ram_addr1));
  Comparator #(.Bits(2)) comparator_5 (.a(mode), .b(2'b00), .eq(comparator_5_eq[0]));  // open: gt, lt
  Add #(.Bits(64)) add_1 (.a(IP), .b({{61{1'b0}}, im_addr}), .c_i(1'b0), .s(write_data));  // open: c_o
  Comparator #(.Bits(2)) comparator_6 (.a(mode), .b(2'b10), .lt(comparator_6_lt));  // open: gt, eq
  Comparator #(.Bits(2)) comparator_7 (.a(2'b10), .b(mode_out), .eq(comparator_7_eq));  // open: gt, lt
  Comparator #(.Bits(2)) comparator_8 (.a(2'b01), .b(mode), .eq(comparator_8_eq));  // open: gt, lt
  Multiplexer #(.Bits(64)) multiplexer_3 (.sel(comparator_8_eq), .in_0(multiplexer_1_out), .in_1(word), .out(im_word));
  Add #(.Bits(2)) add_2 (.a(mode), .b({1'b0, comparator_5_eq[0]}), .c_i(1'b0), .s(add_2_s));  // open: c_o
  and and_2 (im_store, comparator_6_lt, not_1_out);
  not not_1 (not_1_out, write_store);
  Multiplexer #(.Bits(2)) multiplexer_4 (.sel(write_store), .in_0(add_2_s), .in_1(2'b10), .out(mode_out));
  Comparator #(.Bits(2)) comparator_9 (.a(mode), .b(2'b10), .lt(act));  // open: gt, eq

  assign reg_read1 = {8{1'b1}};
  assign write_reg = {8{1'b1}};

  // Notes on the sheet:
  //   If mode is 0, we have to read next instruction (one word only)
endmodule
