// Digital circuit mode-register.dig as structural Verilog
module mode_register (
  input  clock,
  input  [1:0] in,
  output [1:0] mode
);

  Register #(.Bits(2)) register_1 (.D(in), .C(clock), .en(1'b1), .Q(mode));
endmodule
