// Digital circuit ARITHM_OP_MEMreg_reg.dig as structural Verilog
module ARITHM_OP_MEMreg_reg (
  input  act,
  input  [3:0] aopcode,
  input  [7:0] reg1,
  input  [7:0] reg2,
  input  [63:0] in_1,
  input  [63:0] in_2,
  input  [63:0] in_3,
  output [7:0] read_reg1,
  output [7:0] read_reg2,
  output [63:0] read_addr1,
  output [63:0] addr_write,
  output [63:0] data_write,
  output store_write
);

  wire [63:0] arithm_executor_1_x_out;

  arithm_executor arithm_executor_1 (.aopcode(aopcode), .X(in_3), .Y(in_2), .X_out(arithm_executor_1_x_out));
  active_8 active_8_1 (.in(reg1), .act(act), .out(read_reg1));
  active_8 active_8_2 (.in(reg2), .act(act), .out(read_reg2));
  active_64 active_64_1 (.in(in_1), .act(act), .out(addr_write));
  active_64 active_64_2 (.in(arithm_executor_1_x_out), .act(act), .out(data_write));
  active_1 active_1_1 (.in(act), .act(act), .out(store_write));
  active_64 active_64_3 (.in(in_1), .act(act), .out(read_addr1));
endmodule
