// Digital circuit arithm-executor.dig as structural Verilog
module arithm_executor (
  input  [3:0] aopcode,
  input  [63:0] X,
  input  [63:0] Y,
  output [63:0] X_out
);

  wire [63:0] ADD_s, and_1_out, barrelshifter_1_out, barrelshifter_2_out, DIVQ_q, DIVR_r, MUL_mul, not_1_out,
       or_1_out, SUB_s, xor_1_out;

  Add #(.Bits(64)) ADD (.a(X), .b(Y), .c_i(1'b0), .s(ADD_s));  // open: c_o
  Sub #(.Bits(64)) SUB (.a(X), .b(Y), .c_i(1'b0), .s(SUB_s));  // open: c_o
  Mul #(.Signed("true"), .Bits(32)) MUL (.a(X[31:0]), .b(Y[31:0]), .mul(MUL_mul));
  Div #(.Signed("true"), .Bits(64)) DIVQ (.a(X), .b(Y), .q(DIVQ_q));  // open: r
  Div #(.Signed("true"), .Bits(64)) DIVR (.a(X), .b(Y), .r(DIVR_r));  // open: q
  assign and_1_out = X & Y;  // And and_1, 64 bits wide
  assign or_1_out = X | Y;  // Or or_1, 64 bits wide
  assign xor_1_out = X ^ Y;  // XOr xor_1, 64 bits wide
  assign not_1_out = ~X;  // Not not_1, 64 bits wide
  BarrelShifter #(.Bits(64), .barrelShifterMode("arithmetic")) barrelshifter_1 (
    .in(X), .shift(Y[6:0]), .out(barrelshifter_1_out));
  BarrelShifter #(.Bits(64), .barrelShifterMode("arithmetic"), .direction("right")) barrelshifter_2 (
    .in(X), .shift(Y[6:0]), .out(barrelshifter_2_out));
  Multiplexer #(.Selector_Bits(4), .Bits(64)) multiplexer_1 (
    .sel(aopcode), .in_0(ADD_s), .in_1(SUB_s), .in_2(MUL_mul), .in_3(DIVQ_q), .in_4(DIVR_r),
    .in_5(and_1_out), .in_6(or_1_out), .in_7(xor_1_out), .in_8(not_1_out), .in_9(barrelshifter_1_out),
    .in_10(barrelshifter_2_out), .in_11({64{1'b0}}), .in_12({64{1'b0}}), .in_13({64{1'b0}}),
    .in_14({64{1'b0}}), .in_15({64{1'b0}}), .out(X_out));
endmodule
