// Digital circuit CMP-executor.dig as structural Verilog
module CMP_executor (
  input  [63:0] x,
  input  [63:0] y,
  output [63:0] out
);

  wire [0:0] comparator_1_eq, comparator_1_gt, comparator_1_lt, not_1_out, not_2_out, not_3_out;
  wire [63:0] equal_out, greater_equal_out, greater_out, less_equal_out, less_out, not_equal_out;

  Comparator #(.Bits(64), .Signed("true")) comparator_1 (
    .a(x), .b(y), .gt(comparator_1_gt[0]), .eq(comparator_1_eq[0]), .lt(comparator_1_lt[0]));
  not not_1 (not_1_out[0], comparator_1_eq[0]);
  not not_2 (not_2_out[0], comparator_1_gt[0]);
  not not_3 (not_3_out[0], comparator_1_lt[0]);
  BarrelShifter #(.Bits(64), .barrelShifterMode("arithmetic")) equal (
    .in({{63{1'b0}}, comparator_1_eq[0]}), .shift({7{1'b0}}), .out(equal_out));
  BarrelShifter #(.Bits(64), .barrelShifterMode("arithmetic")) not_equal (
    .in({{63{1'b0}}, not_1_out[0]}), .shift(7'b0000001), .out(not_equal_out));
  BarrelShifter #(.Bits(64), .barrelShifterMode("arithmetic")) less (
    .in({{63{1'b0}}, comparator_1_lt[0]}), .shift(7'b0000010), .out(less_out));
  BarrelShifter #(.Bits(64), .barrelShifterMode("arithmetic")) less_equal (
    .in({{63{1'b0}}, not_2_out[0]}), .shift(7'b0000011), .out(less_equal_out));
  BarrelShifter #(.Bits(64), .barrelShifterMode("arithmetic")) greater (
    .in({{63{1'b0}}, comparator_1_gt[0]}), .shift(7'b0000100), .out(greater_out));
  BarrelShifter #(.Bits(64), .barrelShifterMode("arithmetic")) greater_equal (
    .in({{63{1'b0}}, not_3_out[0]}), .shift(7'b0000101), .out(greater_equal_out));
  assign out = equal_out | not_equal_out | less_out | less_equal_out | greater_out | greater_equal_out;  // Or or_1, 64 bits wide
endmodule
