// Digital circuit CMP_reg_const.dig as structural Verilog
module CMP_reg_const (
  input  act,
  input  [7:0] reg1,
  input  [63:0] \const ,
  input  [63:0] in_1,
  output [7:0] read_reg1,
  output [7:0] reg_write,
  output [63:0] data_write,
  output store_write
);

  wire [63:0] cmp_executor_1_out;

  CMP_executor cmp_executor_1 (.x(in_1), .y(\const ), .out(cmp_executor_1_out));
  active_8 active_8_1 (.in(reg1), .act(act), .out(read_reg1));
  active_8 active_8_2 (.in(8'hfc), .act(act), .out(reg_write));
  active_64 active_64_1 (.in(cmp_executor_1_out), .act(act), .out(data_write));
  active_1 active_1_1 (.in(act), .act(act), .out(store_write));
endmodule
