// Digital circuit JMP-executor.dig as structural Verilog
module JMP_executor (
  input  [2:0] condcode,
  input  [63:0] addr,
  input  [63:0] CF,
  output [63:0] IP_out
);

  wire check_bit_1_res, check_bit_2_res, check_bit_3_res, check_bit_4_res, check_bit_5_res, check_bit_6_res;
  wire [63:0] multiplexer_1_out, multiplexer_2_out, multiplexer_3_out, multiplexer_4_out, multiplexer_5_out,
       multiplexer_6_out;

  check_bit check_bit_1 (.x(CF), .\bit ({7{1'b0}}), .res(check_bit_1_res));
  check_bit check_bit_2 (.x(CF), .\bit (7'b0000001), .res(check_bit_2_res));
  check_bit check_bit_3 (.x(CF), .\bit (7'b0000010), .res(check_bit_3_res));
  check_bit check_bit_4 (.x(CF), .\bit (7'b0000011), .res(check_bit_4_res));
  check_bit check_bit_5 (.x(CF), .\bit (7'b0000100), .res(check_bit_5_res));
  check_bit check_bit_6 (.x(CF), .\bit (7'b0000101), .res(check_bit_6_res));
  Multiplexer #(.Bits(64)) multiplexer_1 (
    .sel(check_bit_1_res), .in_0(64'hffffffff), .in_1(addr), .out(multiplexer_1_out));
  Multiplexer #(.Bits(64)) multiplexer_2 (
    .sel(check_bit_2_res), .in_0(64'hffffffff), .in_1(addr), .out(multiplexer_2_out));
  Multiplexer #(.Bits(64)) multiplexer_3 (
    .sel(check_bit_3_res), .in_0(64'hffffffff), .in_1(addr), .out(multiplexer_3_out));
  Multiplexer #(.Bits(64)) multiplexer_4 (
    .sel(check_bit_4_res), .in_0(64'hffffffff), .in_1(addr), .out(multiplexer_4_out));
  Multiplexer #(.Bits(64)) multiplexer_5 (
    .sel(check_bit_5_res), .in_0(64'hffffffff), .in_1(addr), .out(multiplexer_5_out));
  Multiplexer #(.Bits(64)) multiplexer_6 (
    .sel(check_bit_6_res), .in_0(64'hffffffff), .in_1(addr), .out(multiplexer_6_out));
  Multiplexer #(.Selector_Bits(3), .Bits(64)) multiplexer_7 (
    .sel(condcode), .in_0(multiplexer_1_out), .in_1(multiplexer_2_out), .in_2(multiplexer_3_out),
    .in_3(multiplexer_4_out), .in_4(multiplexer_5_out), .in_5(multiplexer_6_out), .in_6(addr),
    .in_7(64'hffffffff), .out(IP_out));
endmodule
