// Digital circuit JMP_CND_const.dig as structural Verilog
module JMP_CND_const (
  input  act,
  input  [2:0] condcode,
  input  [63:0] \const ,
  input  [63:0] CF,
  output [63:0] IP_out,
  output act_out
);

  wire comparator_1_eq, not_1_out;
  wire [63:0] jmp_executor_1_ip_out;

  JMP_executor jmp_executor_1 (.condcode(condcode), .addr(\const ), .CF(CF), .IP_out(jmp_executor_1_ip_out));
  Comparator #(.Bits(64)) comparator_1 (
    .a(64'hffffffff), .b(jmp_executor_1_ip_out), .eq(comparator_1_eq));  // open: gt, lt
  active_64 active_64_1 (.in(jmp_executor_1_ip_out), .act(act), .out(IP_out));
  not not_1 (not_1_out, comparator_1_eq);
  and and_1 (act_out, act, not_1_out);
endmodule
