// Digital circuit check-bit.dig as structural Verilog
module check_bit (
  input  [63:0] x,
  input  [6:0] \bit ,
  output res
);

  wire [6:0] sub_1_s;
  wire [63:0] barrelshifter_1_out;
  wire [63:1] barrelshifter_2_out;

  Sub #(.Bits(7)) sub_1 (.a(7'b0111111), .b(\bit ), .c_i(1'b0), .s(sub_1_s));  // open: c_o
  BarrelShifter #(.Bits(64)) barrelshifter_1 (.in(x), .shift(sub_1_s), .out(barrelshifter_1_out));
  BarrelShifter #(.Bits(64), .direction("right")) barrelshifter_2 (
    .in(barrelshifter_1_out), .shift(7'b0111111), .out({barrelshifter_2_out, res}));
endmodule
