// Digital circuit MOV.dig as structural Verilog
module MOV (
  input  [63:0] word1,
  input  [63:0] word2,
  input  [63:0] word3,
  input  [63:0] reg_in1,
  input  [63:0] reg_in2,
  input  [63:0] ram_in1,
  input  [1:0] mode,
  output act,
  output [7:0] reg_read1,
  output [7:0] reg_read2,
  output [7:0] reg_write,
  output [63:0] reg_data,
  output reg_store,
  output [63:0] RAM_read1,
  output [63:0] RAM_read2,
  output [63:0] RAM_write,
  output [63:0] RAM_data,
  output RAM_store,
  output [1:0] mode_out
);

  wire comparator_1_eq, decoder_1_out_0, decoder_1_out_1, decoder_1_out_2, decoder_1_out_3, decoder_1_out_4,
       decoder_1_out_5, decoder_1_out_6, decoder_1_out_7, mov_memconst_const_1_write_store,
       mov_memconst_reg_1_write_store, mov_memreg_const_1_write_store, mov_memreg_reg_1_write_store,
       mov_reg_const_1_write_store, mov_reg_memconst_1_p8, mov_reg_memreg_1_write_store,
       mov_reg_reg_1_write_store, or_1_out;
  wire [7:0] actual_op_s, mov_memconst_reg_1_read_reg, mov_memreg_const_1_read_reg,
       mov_memreg_reg_1_reg_read1, mov_memreg_reg_1_reg_read2, mov_reg_const_1_write_reg,
       mov_reg_memconst_1_p6, mov_reg_memreg_1_reg_read, mov_reg_memreg_1_write_reg, mov_reg_reg_1_reg_read,
       mov_reg_reg_1_write_reg;
  wire [63:0] mov_memconst_const_1_write_addr, mov_memconst_const_1_write_data,
       mov_memconst_reg_1_write_addr, mov_memconst_reg_1_write_data, mov_memreg_const_1_write_addr,
       mov_memreg_const_1_write_data, mov_memreg_reg_1_write_addr, mov_memreg_reg_1_write_data,
       mov_reg_const_1_write_data, mov_reg_memconst_1_p5, mov_reg_memconst_1_p7, mov_reg_memreg_1_ram_read,
       mov_reg_memreg_1_write_data, mov_reg_reg_1_write_data;

  Sub #(.Bits(8)) actual_op (.a(word1[10:3]), .b({8{1'b0}}), .c_i(1'b0), .s(actual_op_s));  // open: c_o
  Decoder #(.Selector_Bits(8)) decoder_1 (
    .sel(actual_op_s), .out_0(decoder_1_out_0), .out_1(decoder_1_out_1), .out_2(decoder_1_out_2),
    .out_3(decoder_1_out_3), .out_4(decoder_1_out_4), .out_5(decoder_1_out_5), .out_6(decoder_1_out_6),
    .out_7(decoder_1_out_7));  // open: out_8, out_9, out_10, out_11, out_12, out_13, out_14, out_15, out_16, out_17, out_18, out_19, out_20, out_21, out_22, out_23, out_24, out_25, out_26, out_27, out_28, out_29, out_30, out_31, out_32, out_33, out_34, out_35, out_36, out_37, out_38, out_39, out_40, out_41, out_42, out_43, out_44, out_45, out_46, out_47, out_48, out_49, out_50, out_51, out_52, out_53, out_54, out_55, out_56, out_57, out_58, out_59, out_60, out_61, out_62, out_63, out_64, out_65, out_66, out_67, out_68, out_69, out_70, out_71, out_72, out_73, out_74, out_75, out_76, out_77, out_78, out_79, out_80, out_81, out_82, out_83, out_84, out_85, out_86, out_87, out_88, out_89, out_90, out_91, out_92, out_93, out_94, out_95, out_96, out_97, out_98, out_99, out_100, out_101, out_102, out_103, out_104, out_105, out_106, out_107, out_108, out_109, out_110, out_111, out_112, out_113, out_114, out_115, out_116, out_117, out_118, out_119, out_120, out_121, out_122, out_123, out_124, out_125, out_126, out_127, out_128, out_129, out_130, out_131, out_132, out_133, out_134, out_135, out_136, out_137, out_138, out_139, out_140, out_141, out_142, out_143, out_144, out_145, out_146, out_147, out_148, out_149, out_150, out_151, out_152, out_153, out_154, out_155, out_156, out_157, out_158, out_159, out_160, out_161, out_162, out_163, out_164, out_165, out_166, out_167, out_168, out_169, out_170, out_171, out_172, out_173, out_174, out_175, out_176, out_177, out_178, out_179, out_180, out_181, out_182, out_183, out_184, out_185, out_186, out_187, out_188, out_189, out_190, out_191, out_192, out_193, out_194, out_195, out_196, out_197, out_198, out_199, out_200, out_201, out_202, out_203, out_204, out_205, out_206, out_207, out_208, out_209, out_210, out_211, out_212, out_213, out_214, out_215, out_216, out_217, out_218, out_219, out_220, out_221, out_222, out_223, out_224, out_225, out_226, out_227, out_228, out_229, out_230, out_231, out_232, out_233, out_234, out_235, out_236, out_237, out_238, out_239, out_240, out_241, out_242, out_243, out_244, out_245, out_246, out_247, out_248, out_249, out_250, out_251, out_252, out_253, out_254, out_255
  or or_1 (or_1_out, decoder_1_out_0, decoder_1_out_1, decoder_1_out_2, decoder_1_out_3, decoder_1_out_4, decoder_1_out_5, decoder_1_out_6, decoder_1_out_7, 1'b0);
  Comparator #(.Bits(2)) comparator_1 (.a(mode), .b(2'b10), .eq(comparator_1_eq));  // open: gt, lt
  mov_reg_reg mov_reg_reg_1 (
    .act(decoder_1_out_0), .reg_1(word1[18:11]), .reg_2(word1[26:19]), .in(reg_in1),
    .reg_read(mov_reg_reg_1_reg_read), .write_reg(mov_reg_reg_1_write_reg),
    .write_data(mov_reg_reg_1_write_data), .write_store(mov_reg_reg_1_write_store));
  mov_reg_const mov_reg_const_1 (
    .act(decoder_1_out_1), .\reg (word1[18:11]), .\const (word2), .write_reg(mov_reg_const_1_write_reg),
    .write_data(mov_reg_const_1_write_data), .write_store(mov_reg_const_1_write_store));
  // mov_reg_MEMconst mov_reg_memconst_1: pin names not known; wires that end beside it: decoder_1_out_2, word1[18:11], word2, ram_in1, mov_reg_memconst_1_p5, mov_reg_memconst_1_p6, mov_reg_memconst_1_p7, mov_reg_memconst_1_p8
  mov_reg_MEMreg mov_reg_memreg_1 (
    .act(decoder_1_out_3), .reg_1(word1[18:11]), .reg_2(word1[26:19]), .in_1(reg_in1), .in_2(ram_in1),
    .reg_read(mov_reg_memreg_1_reg_read), .ram_read(mov_reg_memreg_1_ram_read),
    .write_reg(mov_reg_memreg_1_write_reg), .write_data(mov_reg_memreg_1_write_data),
    .write_store(mov_reg_memreg_1_write_store));
  mov_MEMconst_const mov_memconst_const_1 (
    .act(decoder_1_out_4), .const_1(word2), .const_2(word3), .write_addr(mov_memconst_const_1_write_addr),
    .write_data(mov_memconst_const_1_write_data), .write_store(mov_memconst_const_1_write_store));
  mov_MEMconst_reg mov_memconst_reg_1 (
    .act(decoder_1_out_5), .\const (word2), .\reg (word1[18:11]), .in(reg_in1),
    .read_reg(mov_memconst_reg_1_read_reg), .write_addr(mov_memconst_reg_1_write_addr),
    .write_data(mov_memconst_reg_1_write_data), .write_store(mov_memconst_reg_1_write_store));
  mov_MEMreg_const mov_memreg_const_1 (
    .act(decoder_1_out_6), .\reg (word1[18:11]), .\const (word2), .in(reg_in1),
    .read_reg(mov_memreg_const_1_read_reg), .write_addr(mov_memreg_const_1_write_addr),
    .write_data(mov_memreg_const_1_write_data), .write_store(mov_memreg_const_1_write_store));
  mov_MEMreg_reg mov_memreg_reg_1 (
    .act(decoder_1_out_7), .reg_1(word1[18:11]), .reg_2(word1[26:19]), .in_1(reg_in1), .in_2(reg_in2),
    .reg_read1(mov_memreg_reg_1_reg_read1), .reg_read2(mov_memreg_reg_1_reg_read2),
    .write_addr(mov_memreg_reg_1_write_addr), .write_data(mov_memreg_reg_1_write_data),
    .write_store(mov_memreg_reg_1_write_store));
  assign reg_read1 = mov_reg_reg_1_reg_read | mov_reg_memreg_1_reg_read | mov_memconst_reg_1_read_reg | mov_memreg_const_1_read_reg | mov_memreg_reg_1_reg_read1;  // Or or_2, 8 bits wide
  assign reg_read2 = mov_memreg_reg_1_reg_read2 | {8{1'b0}} | {8{1'b0}} | {8{1'b0}} | {8{1'b0}};  // Or or_3, 8 bits wide
  assign reg_write = mov_reg_reg_1_write_reg | mov_reg_const_1_write_reg | mov_reg_memconst_1_p6 | mov_reg_memreg_1_write_reg | {8{1'b0}};  // Or or_4, 8 bits wide
  assign reg_data = mov_reg_reg_1_write_data | mov_reg_const_1_write_data | mov_reg_memconst_1_p7 | mov_reg_memreg_1_write_data | {64{1'b0}};  // Or or_5, 64 bits wide
  or or_6 (reg_store, mov_reg_reg_1_write_store, mov_reg_const_1_write_store, mov_reg_memconst_1_p8, mov_reg_memreg_1_write_store, 1'b0);
  assign RAM_read1 = mov_reg_memconst_1_p5 | mov_reg_memreg_1_ram_read | {64{1'b0}} | {64{1'b0}} | {64{1'b0}};  // Or or_7, 64 bits wide
  assign RAM_read2 = {64{1'b0}} | {64{1'b0}} | {64{1'b0}} | {64{1'b0}} | {64{1'b0}};  // Or or_8, 64 bits wide
  assign RAM_write = mov_memconst_const_1_write_addr | mov_memconst_reg_1_write_addr | mov_memreg_const_1_write_addr | mov_memreg_reg_1_write_addr | {64{1'b0}};  // Or or_9, 64 bits wide
  assign RAM_data = mov_memconst_const_1_write_data | mov_memconst_reg_1_write_data | mov_memreg_const_1_write_data | mov_memreg_reg_1_write_data | {64{1'b0}};  // Or or_10, 64 bits wide
  or or_11 (RAM_store, mov_memconst_const_1_write_store, mov_memconst_reg_1_write_store, mov_memreg_const_1_write_store, mov_memreg_reg_1_write_store, 1'b0);
  and and_1 (act, comparator_1_eq, or_1_out);
  Multiplexer #(.Bits(2)) multiplexer_1 (.sel(act), .in_0(2'b10), .in_1(2'b00), .out(mode_out));
endmodule
