// Digital circuit mov_MEMconst_const.dig as structural Verilog
module mov_MEMconst_const (
  input  act,
  input  [63:0] const_1,
  input  [63:0] const_2,
  output [63:0] write_addr,
  output [63:0] write_data,
  output write_store
);

  active_64 active_64_1 (.in(const_1), .act(act), .out(write_addr));
  active_64 active_64_2 (.in(const_2), .act(act), .out(write_data));
  active_1 active_1_1 (.in(act), .act(act), .out(write_store));
endmodule
