// Digital circuit mov_MEMconst_reg.dig as structural Verilog
module mov_MEMconst_reg (
  input  act,
  input  [63:0] \const ,
  input  [7:0] \reg ,
  input  [63:0] in,
  output [7:0] read_reg,
  output [63:0] write_addr,
  output [63:0] write_data,
  output write_store
);

  active_8 active_8_1 (.in(\reg ), .act(act), .out(read_reg));
  active_64 active_64_1 (.in(\const ), .act(act), .out(write_addr));
  active_64 active_64_2 (.in(in), .act(act), .out(write_data));
  active_1 active_1_1 (.in(act), .act(act), .out(write_store));
endmodule
