// Digital circuit mov_MEMreg_reg.dig as structural Verilog
module mov_MEMreg_reg (
  input  act,
  input  [7:0] reg_1,
  input  [7:0] reg_2,
  input  [63:0] in_1,
  input  [63:0] in_2,
  output [7:0] reg_read1,
  output [7:0] reg_read2,
  output [63:0] write_addr,
  output [63:0] write_data,
  output write_store
);

  active_8 active_8_1 (.in(reg_1), .act(act), .out(reg_read1));
  active_8 active_8_2 (.in(reg_2), .act(act), .out(reg_read2));
  active_64 active_64_1 (.in(in_1), .act(act), .out(write_addr));
  active_64 active_64_2 (.in(in_2), .act(act), .out(write_data));
  active_1 active_1_1 (.in(act), .act(act), .out(write_store));
endmodule
