// Digital circuit mov_reg_MEMconst.dig as structural Verilog
module mov_reg_MEMconst (
  input  act,
  input  [7:0] \reg ,
  input  [63:0] \const ,
  input  [63:0] in,
  output [7:0] ram_read,
  output [7:0] write_reg,
  output [63:0] write_data,
  output write_store
);

  // active_64 active_64_1: pin names not known; wires that end beside it: \const , act, ram_read
  active_8 active_8_1 (.in(\reg ), .act(act), .out(write_reg));
  active_64 active_64_2 (.in(in), .act(act), .out(write_data));
  active_1 active_1_1 (.in(act), .act(act), .out(write_store));
endmodule
