// Digital circuit mov_reg_const.dig as structural Verilog
module mov_reg_const (
  input  act,
  input  [7:0] \reg ,
  input  [63:0] \const ,
  output [7:0] write_reg,
  output [63:0] write_data,
  output write_store
);

  active_8 active_8_1 (.in(\reg ), .act(act), .out(write_reg));
  active_64 active_64_1 (.in(\const ), .act(act), .out(write_data));
  active_1 active_1_1 (.in(act), .act(act), .out(write_store));
endmodule
