// Digital circuit mov_reg_reg.dig as structural Verilog
module mov_reg_reg (
  input  act,
  input  [7:0] reg_1,
  input  [7:0] reg_2,
  input  [63:0] in,
  output [7:0] reg_read,
  output [7:0] write_reg,
  output [63:0] write_data,
  output write_store
);

  active_8 active_8_1 (.in(reg_2), .act(act), .out(reg_read));
  active_8 active_8_2 (.in(reg_1), .act(act), .out(write_reg));
  active_64 active_64_1 (.in(in), .act(act), .out(write_data));
  active_1 active_1_1 (.in(act), .act(act), .out(write_store));
endmodule
