// Digital circuit instruction-memory.dig as structural Verilog
module instruction_memory (
  input  [2:0] word_write,
  input  [63:0] data_write,
  input  store_write,
  input  clock,
  output [63:0] word1,
  output [63:0] word2,
  output [63:0] word3,
  output [63:0] word4,
  output [63:0] word5,
  output [63:0] word6,
  output [63:0] word7,
  output [63:0] word8
);

  wire demultiplexer_1_out_0, demultiplexer_1_out_1, demultiplexer_1_out_2, demultiplexer_1_out_3,
       demultiplexer_1_out_4, demultiplexer_1_out_5, demultiplexer_1_out_6, demultiplexer_1_out_7;
  wire [63:0] demultiplexer_2_out_0, demultiplexer_2_out_1, demultiplexer_2_out_2, demultiplexer_2_out_3,
       demultiplexer_2_out_4, demultiplexer_2_out_5, demultiplexer_2_out_6, demultiplexer_2_out_7;

  Demultiplexer #(.Selector_Bits(3)) demultiplexer_1 (
    .sel(word_write), .in(store_write), .out_0(demultiplexer_1_out_0), .out_1(demultiplexer_1_out_1),
    .out_2(demultiplexer_1_out_2), .out_3(demultiplexer_1_out_3), .out_4(demultiplexer_1_out_4),
    .out_5(demultiplexer_1_out_5), .out_6(demultiplexer_1_out_6), .out_7(demultiplexer_1_out_7));
  Demultiplexer #(.Selector_Bits(3), .Bits(64)) demultiplexer_2 (
    .sel(word_write), .in(data_write), .out_0(demultiplexer_2_out_0), .out_1(demultiplexer_2_out_1),
    .out_2(demultiplexer_2_out_2), .out_3(demultiplexer_2_out_3), .out_4(demultiplexer_2_out_4),
    .out_5(demultiplexer_2_out_5), .out_6(demultiplexer_2_out_6), .out_7(demultiplexer_2_out_7));
  Register #(.Bits(64)) u_word1 (.D(demultiplexer_2_out_0), .C(clock), .en(demultiplexer_1_out_0), .Q(word1));
  Register #(.Bits(64)) u_word2 (.D(demultiplexer_2_out_1), .C(clock), .en(demultiplexer_1_out_1), .Q(word2));
  Register #(.Bits(64)) u_word3 (.D(demultiplexer_2_out_2), .C(clock), .en(demultiplexer_1_out_2), .Q(word3));
  Register #(.Bits(64)) u_word4 (.D(demultiplexer_2_out_3), .C(clock), .en(demultiplexer_1_out_3), .Q(word4));
  Register #(.Bits(64)) u_word5 (.D(demultiplexer_2_out_4), .C(clock), .en(demultiplexer_1_out_4), .Q(word5));
  Register #(.Bits(64)) u_word6 (.D(demultiplexer_2_out_5), .C(clock), .en(demultiplexer_1_out_5), .Q(word6));
  Register #(.Bits(64)) u_word7 (.D(demultiplexer_2_out_6), .C(clock), .en(demultiplexer_1_out_6), .Q(word7));
  Register #(.Bits(64)) u_word8 (.D(demultiplexer_2_out_7), .C(clock), .en(demultiplexer_1_out_7), .Q(word8));
endmodule
