// Digital circuit ram.dig as structural Verilog
module ram (
  input  [63:0] addr_read1,
  input  [63:0] addr_read2,
  input  [63:0] addr_write,
  input  [63:0] data_write,
  input  store_write,
  input  clock,
  output [63:0] res_read1,
  output [63:0] res_read2
);

  RegisterFile #(.AddrBits(24), .Bits(64)) registerfile_1 (
    .Din(data_write), .we(store_write), .Rw(addr_write[23:0]), .C(clock), .Ra(addr_read1[23:0]),
    .Rb(addr_read2[23:0]), .Da(res_read1), .Db(res_read2));
endmodule
