// Digital circuit registers.dig as structural Verilog
module registers (
  input  [7:0] reg_read1,
  input  [7:0] reg_read2,
  input  [7:0] reg_write,
  input  [63:0] data_write,
  input  store_write,
  input  clock,
  output [63:0] res_read1,
  output [63:0] res_read2
);

  RegisterFile #(.AddrBits(8), .Bits(64)) Registers (
    .Din(data_write), .we(store_write), .Rw(reg_write), .C(clock), .Ra(reg_read1), .Rb(reg_read2),
    .Da(res_read1), .Db(res_read2));
endmodule
